// Logisim project ALU.circ as structural Verilog: 1 circuit, main circuit ALU
module ALU (
  input  [31:0] A,
  input  [31:0] B,
  input  [4:0] Shift,
  input  CarryIn,
  input  [3:0] Codop,
  output [3:0] Flags,
  output [31:0] S
);

  wire adder_3_cout, adder_4_cout, adder_5_cout, and_4_out, and_5_out, bitselector_1_out, bitselector_2_out,
       bitselector_3_out, not_2_out, not_3_out, not_4_out, subtractor_4_bout, subtractor_5_bout, xor_2_out,
       xor_3_out;
  wire [4:0] bitfinder_1_index, bitfinder_2_index;
  wire [31:0] adder_1_out, adder_2_out, and_1_out, and_2_out, and_3_out, multiplier_1_out, not_1_out,
       or_1_out, shifter_1_out, shifter_2_out, shifter_3_out, shifter_4_out, subtractor_1_out,
       subtractor_2_out, subtractor_3_out, xor_1_out;

  assign not_1_out = ~B;  // NOT_Gate not_1, 32 bits wide
  not not_2 (not_2_out, CarryIn);
  assign and_1_out = A & B;  // AND_Gate and_1, 32 bits wide
  assign xor_1_out = A ^ B;  // XOR_Gate xor_1, 32 bits wide
  Shifter #(.width(32)) shifter_1 (.in(B), .\dist (Shift), .out(shifter_1_out));
  Shifter #(.shift("lr"), .width(32)) shifter_2 (.in(B), .\dist (Shift), .out(shifter_2_out));
  Shifter #(.shift("ar"), .width(32)) shifter_3 (.in(B), .\dist (Shift), .out(shifter_3_out));
  Adder #(.width(32)) adder_1 (.a(A), .b(B), .out(adder_1_out), .cin(CarryIn));  // open: cout
  Subtractor #(.width(32)) subtractor_1 (.a(B), .b(A), .out(subtractor_1_out), .bin(not_2_out));  // open: bout
  Shifter #(.shift("rr"), .width(32)) shifter_4 (.in(B), .\dist (Shift), .out(shifter_4_out));
  assign and_2_out = A & B;  // AND_Gate and_2, 32 bits wide
  Subtractor #(.width(32)) subtractor_2 (.a({32{1'b0}}), .b(A), .out(subtractor_2_out));  // open: bin, bout
  Subtractor #(.width(32)) subtractor_3 (.a(B), .b(A), .out(subtractor_3_out));  // open: bin, bout
  Adder #(.width(32)) adder_2 (.a(A), .b(B), .out(adder_2_out));  // open: cin, cout
  assign or_1_out = A | B;  // OR_Gate or_1, 32 bits wide
  Multiplier #(.width(32)) multiplier_1 (.a(A), .b(B), .out(multiplier_1_out));  // open: cin, cout
  assign and_3_out = A & not_1_out;  // AND_Gate and_3, 32 bits wide
  Multiplexer #(.enable("false"), .select(4), .width(32)) multiplexer_1 (
    .in0(and_1_out), .in1(xor_1_out), .in2(shifter_1_out), .in3(shifter_2_out), .in4(shifter_3_out),
    .in5(adder_1_out), .in6(subtractor_1_out), .in7(shifter_4_out), .in8(and_2_out), .in9(subtractor_2_out),
    .in10(subtractor_3_out), .in11(adder_2_out), .in12(or_1_out), .in13(multiplier_1_out), .in14(and_3_out),
    .in15(not_1_out), .out(S), .sel(Codop));
  // Probe on Flags[1]
  Multiplexer #(.enable("false"), .select(4)) multiplexer_2 (
    .in0(1'b0), .in1(1'b0), .in2(adder_5_cout), .in3(not_4_out), .in4(not_4_out), .in5(adder_4_cout),
    .in6(1'b0), .in7(not_4_out), .in8(1'b0), .in9(1'b0), .in10(not_3_out), .in11(adder_3_cout), .in12(1'b0),
    .in13(1'b0), .in14(1'b0), .in15(1'b0), .out(Flags[1]), .sel(Codop));
  Comparator #(.width(32)) comparator_1 (.a(S), .b({32{1'b0}}), .eq(Flags[2]), .lt(Flags[3]));  // open: gt
  Subtractor #(.width(32)) subtractor_4 (.a(B), .b(A), .bout(subtractor_4_bout));  // open: out, bin
  Adder #(.width(32)) adder_3 (.a(A), .b(B), .cout(adder_3_cout));  // open: out, cin
  BitFinder #(.\type ("high1"), .width(32)) bitfinder_1 (.in(B), .index(bitfinder_1_index));  // open: found
  BitFinder #(.width(32)) bitfinder_2 (.in(B), .index(bitfinder_2_index));  // open: found
  Adder #(.width(32)) adder_4 (.a(A), .b(B), .cin(CarryIn), .cout(adder_4_cout));  // open: out
  not not_3 (not_3_out, subtractor_4_bout);
  Subtractor #(.width(5)) subtractor_5 (.a(bitfinder_2_index), .b(Shift), .bout(subtractor_5_bout));  // open: out, bin
  not not_4 (not_4_out, subtractor_5_bout);
  Adder #(.width(5)) adder_5 (.a(bitfinder_1_index), .b(Shift), .cout(adder_5_cout));  // open: out, cin
  // Probe on Flags[0]
  Multiplexer #(.enable("false"), .select(4)) multiplexer_3 (
    .in0(1'b0), .in1(1'b0), .in2(1'b0), .in3(1'b0), .in4(1'b0), .in5(and_4_out), .in6(and_5_out), .in7(1'b0),
    .in8(1'b0), .in9(1'b0), .in10(and_5_out), .in11(and_4_out), .in12(1'b0), .in13(1'b0), .in14(1'b0),
    .in15(1'b0), .out(Flags[0]), .sel(Codop));
  BitSelector #(.width(32)) bitselector_1 (.in(A), .out(bitselector_1_out), .sel({5{1'b1}}));
  BitSelector #(.width(32)) bitselector_2 (.in(B), .out(bitselector_2_out), .sel({5{1'b1}}));
  BitSelector #(.width(32)) bitselector_3 (.in(S), .out(bitselector_3_out), .sel({5{1'b1}}));
  xor xor_2 (xor_2_out, bitselector_1_out, bitselector_2_out);
  xor xor_3 (xor_3_out, xor_2_out, bitselector_3_out);
  and and_4 (and_4_out, ~xor_2_out, xor_3_out);  // AND_Gate
  and and_5 (and_5_out, ~xor_3_out, xor_2_out);  // AND_Gate

  // Other names for the same wires on the sheet: V = Flags[0]; C = Flags[1]; Z = Flags[2]; N = Flags[3]

  // Notes on the sheet:
  //   Note: for ROR, C = N
  //   Note 2: assume that shift > 0 for LSL and LSR
endmodule
