// Logisim project Ctl_Load_Store.circ as structural Verilog: 1 circuit, main circuit Load_Store
module Load_Store (
  input  Enable,
  input  [15:0] Instruction,
  input  Clk,
  input  Reset,
  input  [31:0] Stack_Pointer,
  output Store,
  output Load,
  output PC_Hold,
  output [2:0] Rmd,
  output [31:0] RAM_Addr
);

  wire and_1_out, d_ff_1_q, demultiplexer_1_out0, demultiplexer_1_out1, multiplexer_1_out, not_1_out;
  wire [31:0] adder_1_out, bit_extender_1_out;

  assign bit_extender_1_out = {{24{1'b0}}, Instruction[7:0]};  // Bit_Extender bit_extender_1
  Adder #(.width(32)) adder_1 (.a(Stack_Pointer), .b(bit_extender_1_out), .out(adder_1_out));  // open: cin, cout
  not not_1 (not_1_out, d_ff_1_q);
  D_Flip_Flop #(.trigger("falling")) d_ff_1 (
    .D(not_1_out), .clk(Clk), .Q(d_ff_1_q), .reset(Reset));  // open: Qn, preset
  Demultiplexer demultiplexer_1 (
    .out0(demultiplexer_1_out0), .out1(demultiplexer_1_out1), .in(1'b1), .sel(Instruction[11]));
  Multiplexer multiplexer_1 (.in0(demultiplexer_1_out1), .in1(1'b0), .out(multiplexer_1_out), .sel(d_ff_1_q));
  and and_1 (and_1_out, demultiplexer_1_out1, d_ff_1_q);
  Multiplexer multiplexer_2 (.in0(1'b0), .in1(demultiplexer_1_out0), .out(Store), .sel(Enable));
  Multiplexer multiplexer_3 (.in0(1'b0), .in1(multiplexer_1_out), .out(Load), .sel(Enable));
  Multiplexer multiplexer_4 (.in0(1'b0), .in1(and_1_out), .out(PC_Hold), .sel(Enable));
  Multiplexer #(.width(3)) multiplexer_5 (.in0(3'b000), .in1(Instruction[10:8]), .out(Rmd), .sel(Enable));
  Multiplexer #(.width(32)) multiplexer_6 (.in0({32{1'b0}}), .in1(adder_1_out), .out(RAM_Addr), .sel(Enable));

  // Notes on the sheet:
  //   Instruction: pull=down
  //   Delay load and hold PC for 1 cycle for the RAM to send out requested data 
endmodule
